// Logisim project sensor_actuator_logic_gates.circ as structural Verilog: 1 circuit, main circuit main
module main (
  input  ER,
  input  DSBF,
  input  DC,
  input  BP,
  input  CM,
  input  DOS,
  input  KIC,
  input  DCL,
  output BELL,
  output BA,
  output DLA
);

  wire and_1_out, and_2_out, and_3_out, and_4_out, and_5_out, not_1_out, not_2_out, not_3_out, not_4_out,
       not_5_out, not_6_out;

  not not_1 (not_1_out, DC);
  not not_2 (not_2_out, DSBF);
  not not_3 (not_3_out, DC);
  not not_4 (not_4_out, KIC);
  not not_5 (not_5_out, DOS);
  not not_6 (not_6_out, KIC);
  and and_1 (and_1_out, ER, DSBF, not_1_out);
  and and_2 (and_2_out, ER, ER, not_2_out, not_3_out);
  and and_3 (and_3_out, DOS, KIC, DCL);
  and and_4 (and_4_out, DOS, not_4_out, DCL);
  and and_5 (and_5_out, not_5_out, not_6_out, DCL);
  or or_1 (BELL, and_1_out, and_2_out);
  or or_2 (DLA, and_3_out, and_4_out, and_5_out);
  and and_6 (BA, BP, CM);

  // Notes on the sheet:
  //   3.4ns + 3.4ns + 3.4ns = 10.2ns
  //   Even with some wire delay,
  //   this is still a fast implementation
  //   3.4ns + 3.4ns + 3.4ns = 10.2ns
  //   Even with some wire delay
  //   this is still a fast implementation
  //   Has a delay of 3.4ns at best.
  //   Has 46.6ns of buffer to meet
  //   the requirement
endmodule
